// Logisim project PROJETO EM ANDAMENTO - Copia.circ as structural Verilog: 6 circuits, main circuit main
module main (
  input  A3,
  input  A2,
  input  A1,
  input  A0,
  input  B3,
  input  B2,
  input  B1,
  input  B0,
  input  in_9,
  input  in_10,
  input  [3:0] \OPERAÇÕES ,
  output [3:0] RESULTADO
);

  wire [3:0] and_1_out_9, or_1_out_9, somador_1_out_11, subtrator_1_out_11, xor_1_out_9;

  Somador somador_1 (
    .Cin(in_9), .B3(B3), .B2(B2), .B1(B1), .B0(B0), .A3(A3), .A2(A2), .A1(A1), .A0(A0),
    .out_11(somador_1_out_11));  // open: Cout
  Subtrator subtrator_1 (
    .Cin(in_10), .B0(B3), .B1(B2), .B2(B1), .B3(B0), .A0(A3), .A1(A2), .A2(A1), .A3(A0),
    .out_11(subtrator_1_out_11));  // open: Cout
  AND and_1 (.A0(A0), .B0(B0), .A1(A1), .B1(B1), .A2(A2), .B2(B2), .A3(A3), .B3(B3), .out_9(and_1_out_9));
  OR or_1 (.A0(A0), .B0(B0), .A1(A1), .B1(B1), .A2(A2), .B2(B2), .A3(A3), .B3(B3), .out_9(or_1_out_9));
  XOR xor_1 (.A0(A0), .B0(B0), .A1(A1), .B1(B1), .A2(A2), .B2(B2), .A3(A3), .B3(B3), .out_9(xor_1_out_9));
  Multiplexer #(.select(4), .width(4), .enable("false")) multiplexer_1 (
    .in0(somador_1_out_11), .in1(subtrator_1_out_11), .in2(and_1_out_9), .in3(or_1_out_9), .in4(xor_1_out_9),
    .out(RESULTADO), .sel(\OPERAÇÕES ));  // open: in5, in6, in7, in8, in9, in10, in11, in12, in13, in14, in15
endmodule

// ADIÇÃO - 0000
module Somador (
  input  A3,
  input  A2,
  input  A1,
  input  A0,
  input  B3,
  input  B2,
  input  B1,
  input  B0,
  input  Cin,
  output Cout,
  output [3:0] out_11
);

  wire and_1_out, and_2_out, and_3_out, and_4_out, and_5_out, and_6_out, and_7_out, and_8_out, or_1_out,
       or_2_out, or_3_out, xor_1_out, xor_3_out, xor_5_out, xor_7_out;

  xor xor_1 (xor_1_out, A0, B0);
  and and_1 (and_1_out, xor_1_out, Cin);
  and and_2 (and_2_out, A0, B0);
  xor xor_2 (out_11[0], xor_1_out, Cin);
  or or_1 (or_1_out, and_1_out, and_2_out);
  xor xor_3 (xor_3_out, A1, B1);
  and and_3 (and_3_out, xor_3_out, or_1_out);
  and and_4 (and_4_out, A1, B1);
  xor xor_4 (out_11[1], xor_3_out, or_1_out);
  or or_2 (or_2_out, and_3_out, and_4_out);
  xor xor_5 (xor_5_out, A2, B2);
  xor xor_6 (out_11[2], xor_5_out, or_2_out);
  and and_5 (and_5_out, xor_5_out, or_2_out);
  and and_6 (and_6_out, A2, B2);
  or or_3 (or_3_out, and_5_out, and_6_out);
  xor xor_7 (xor_7_out, A3, B3);
  and and_7 (and_7_out, xor_7_out, or_3_out);
  and and_8 (and_8_out, A3, A3);
  xor xor_8 (out_11[3], xor_7_out, or_3_out);
  or or_4 (Cout, and_7_out, and_8_out);
endmodule

// SUBTRAIR - 0001
module Subtrator (
  input  A0,
  input  A1,
  input  A2,
  input  A3,
  input  B0,
  input  B1,
  input  B2,
  input  B3,
  input  Cin,
  output Cout,
  output [3:0] out_11
);

  wire and_1_out, and_2_out, and_3_out, and_4_out, and_5_out, and_6_out, and_7_out, and_8_out, not_1_out,
       not_2_out, not_3_out, not_4_out, not_5_out, not_6_out, not_7_out, not_8_out, or_1_out, or_2_out,
       or_3_out, xor_1_out, xor_3_out, xor_5_out, xor_7_out;

  not not_1 (not_1_out, A3);
  xor xor_1 (xor_1_out, A3, B3);
  and and_1 (and_1_out, not_1_out, B3);
  not not_2 (not_2_out, xor_1_out);
  xor xor_2 (out_11[0], xor_1_out, Cin);
  and and_2 (and_2_out, Cin, not_2_out);
  xor xor_3 (xor_3_out, A2, B2);
  not not_3 (not_3_out, A2);
  and and_3 (and_3_out, not_3_out, B2);
  or or_1 (or_1_out, and_2_out, and_1_out);
  not not_4 (not_4_out, xor_3_out);
  xor xor_4 (out_11[1], xor_3_out, or_1_out);
  and and_4 (and_4_out, or_1_out, not_4_out);
  not not_5 (not_5_out, A1);
  or or_2 (or_2_out, and_4_out, and_3_out);
  xor xor_5 (xor_5_out, A1, B1);
  and and_5 (and_5_out, not_5_out, B1);
  not not_6 (not_6_out, xor_5_out);
  xor xor_6 (out_11[2], xor_5_out, or_2_out);
  and and_6 (and_6_out, or_2_out, not_6_out);
  or or_3 (or_3_out, and_6_out, and_5_out);
  not not_7 (not_7_out, A0);
  xor xor_7 (xor_7_out, A0, B0);
  and and_7 (and_7_out, not_7_out, B0);
  not not_8 (not_8_out, xor_7_out);
  xor xor_8 (out_11[3], xor_7_out, or_3_out);
  and and_8 (and_8_out, or_3_out, not_8_out);
  or or_4 (Cout, and_8_out, and_7_out);
endmodule

// AND - 0010
module AND (
  input  A0,
  input  B0,
  input  A1,
  input  B1,
  input  A2,
  input  B2,
  input  A3,
  input  B3,
  output [3:0] out_9
);

  and and_1 (out_9[0], A0, B0);
  and and_2 (out_9[1], A1, B1);
  and and_3 (out_9[2], A2, B2);
  and and_4 (out_9[3], A3, B3);
endmodule

// OR - 0011
module OR (
  input  A0,
  input  B0,
  input  A1,
  input  B1,
  input  A2,
  input  B2,
  input  A3,
  input  B3,
  output [3:0] out_9
);

  or or_1 (out_9[0], A0, B0);
  or or_2 (out_9[1], A1, B1);
  or or_3 (out_9[2], A2, B2);
  or or_4 (out_9[3], A3, B3);
endmodule

// XOR - 0100
module XOR (
  input  A0,
  input  B0,
  input  A1,
  input  B1,
  input  A2,
  input  B2,
  input  A3,
  input  B3,
  output [3:0] out_9
);

  xor xor_1 (out_9[0], A0, B0);
  xor xor_2 (out_9[1], A1, B1);
  xor xor_3 (out_9[2], A2, B2);
  xor xor_4 (out_9[3], A3, B3);
endmodule
